# Fritzing sketch DroneFinderFritzingDiagram with Electron (saved by Fritzing 0.9.2b)
breadboards: 1

parts:
  Part1 = Photon  # not connected
  GPS1 = Adafruit Ultimate GPS Breakout

nets:
  N1: GPS1.3.3V, GPS1.EN, GPS1.VBAT
  GND: GPS1.RX, GPS1.GND, GPS1.VIN, GPS1.PPS
